// Digital circuit ALU.dig as structural Verilog
module ALU (
  input  [15:0] a1,
  input  [15:0] a2,
  input  neg,
  input  [3:0] com,
  output [15:0] o1
);

  wire and_1_out, and_2_out, comparator_1_eq, comparator_2_gt, comparator_3_lt, multiplexer_1_out,
       multiplexer_2_out, multiplexer_3_out, not_1_out, or_3_out, sub_1_c_o;
  wire [7:0] sub_1_s, sub_2_s;
  wire [15:0] add_1_s, add_2_s, add_3_s, and_3_out, demultiplexer_1_out_3, demultiplexer_1_out_3_2,
       demultiplexer_1_out_4, demultiplexer_1_out_4_2, demultiplexer_1_out_5, demultiplexer_1_out_5_2,
       demultiplexer_1_out_6, demultiplexer_1_out_6_2, demultiplexer_1_out_8, demultiplexer_1_out_8_2,
       multiplexer_4_out, multiplexer_5_out, multiplexer_7_out, neg_1_out, not_2_out, or_1_out, or_2_out;
  wire [31:0] demultiplexer_1_out_1, demultiplexer_1_out_2, demultiplexer_1_out_7;

  Demultiplexer #(.Selector_Bits(4), .Bits(32)) demultiplexer_1 (
    .sel(com), .in({a2, a1}), .out_1(demultiplexer_1_out_1), .out_2(demultiplexer_1_out_2),
    .out_3({demultiplexer_1_out_3_2, demultiplexer_1_out_3}),
    .out_4({demultiplexer_1_out_4_2, demultiplexer_1_out_4}),
    .out_5({demultiplexer_1_out_5_2, demultiplexer_1_out_5}),
    .out_6({demultiplexer_1_out_6_2, demultiplexer_1_out_6}), .out_7(demultiplexer_1_out_7),
    .out_8({demultiplexer_1_out_8_2, demultiplexer_1_out_8}));  // open: out_0, out_9, out_10, out_11, out_12, out_13, out_14, out_15
  and and_1 (and_1_out, not_1_out, com[1], com[0]);
  not not_1 (not_1_out, com[2]);
  and and_2 (and_2_out, com[0], com[1], com[2]);
  Comparator #(.Signed("true"), .Bits(16)) comparator_1 (
    .a(demultiplexer_1_out_3), .b(demultiplexer_1_out_3_2), .eq(comparator_1_eq));  // open: gt, lt
  Comparator #(.Signed("true"), .Bits(16)) comparator_2 (
    .a(demultiplexer_1_out_5), .b(demultiplexer_1_out_5_2), .gt(comparator_2_gt));  // open: eq, lt
  Comparator #(.Signed("true"), .Bits(16)) comparator_3 (
    .a(demultiplexer_1_out_6), .b(demultiplexer_1_out_6_2), .lt(comparator_3_lt));  // open: gt, eq
  Multiplexer multiplexer_1 (.sel(and_1_out), .in_0(1'b0), .in_1(comparator_1_eq), .out(multiplexer_1_out));
  Multiplexer multiplexer_2 (.sel(neg), .in_0(comparator_2_gt), .in_1(1'b0), .out(multiplexer_2_out));
  Multiplexer multiplexer_3 (.sel(neg), .in_0(comparator_3_lt), .in_1(1'b0), .out(multiplexer_3_out));
  assign or_1_out = demultiplexer_1_out_8 | demultiplexer_1_out_8_2;  // Or or_1, 16 bits wide
  Add #(.Bits(16)) add_1 (
    .a(demultiplexer_1_out_7[15:0]), .b(demultiplexer_1_out_7[31:16]), .c_i(1'b0), .s(add_1_s));  // open: c_o
  Add #(.Bits(16)) add_2 (
    .a(demultiplexer_1_out_1[15:0]), .b(demultiplexer_1_out_1[31:16]), .c_i(1'b0), .s(add_2_s));  // open: c_o
  Sub #(.Bits(8)) sub_1 (
    .a(demultiplexer_1_out_2[7:0]), .b(demultiplexer_1_out_2[23:16]), .c_i(1'b0), .s(sub_1_s), .c_o(sub_1_c_o));
  Sub #(.Bits(8)) sub_2 (
    .a(demultiplexer_1_out_2[15:8]), .b(demultiplexer_1_out_2[31:24]), .c_i(sub_1_c_o), .s(sub_2_s));  // open: c_o
  assign and_3_out = demultiplexer_1_out_4 & demultiplexer_1_out_4_2;  // And and_3, 16 bits wide
  assign not_2_out = ~add_1_s;  // Not not_2, 16 bits wide
  Multiplexer #(.Bits(16)) multiplexer_4 (.sel(and_2_out), .in_0(add_1_s), .in_1(not_2_out), .out(multiplexer_4_out));
  Multiplexer #(.Bits(16)) multiplexer_5 (.sel(and_2_out), .in_0({16{1'b0}}), .in_1(16'h2), .out(multiplexer_5_out));
  Add #(.Bits(16)) add_3 (.a(multiplexer_5_out), .b(multiplexer_4_out), .c_i(1'b0), .s(add_3_s));  // open: c_o
  assign or_2_out = add_2_s | add_3_s | {sub_2_s, sub_1_s} | or_1_out | and_3_out | multiplexer_7_out;  // Or or_2, 16 bits wide
  or or_3 (or_3_out, multiplexer_1_out, multiplexer_2_out, multiplexer_3_out);
  Neg #(.Bits(16)) neg_1 (.in(or_2_out), .out(neg_1_out));
  Multiplexer #(.Bits(16)) multiplexer_6 (.sel(neg), .in_0(or_2_out), .in_1(neg_1_out), .out(o1));
  Multiplexer #(.Bits(16)) multiplexer_7 (.sel(or_3_out), .in_0({16{1'b0}}), .in_1(16'h1), .out(multiplexer_7_out));
endmodule
