// Digital circuit CPU_Base.dig as structural Verilog
module CPU_Base (
  input  Load,
  input  [1:0] Write_Reg,
  input  [1:0] In_Reg_1,
  input  In_Reg_1_True,
  input  [15:0] In_Num_1,
  input  [1:0] In_Reg_2,
  input  In_Reg_1_True_2,
  input  Negate,
  input  Add,
  input  Subtract,
  input  And,
  input  Or,
  input  [2:0] Jump,
  input  clk,
  input  in_FromMem_1__True,
  input  in_FromMem_1__True_2,
  input  in_Memout_1__True,
  input  in_Memout_1__True_2,
  output [15:0] reg1,
  output [15:0] reg2,
  output [15:0] reg3,
  output [15:0] inMem,
  output [15:0] memory,
  output [15:0] PC,
  output [36:0] out_21,
  output [15:0] out_23,
  output [15:0] out_27,
  output out_28
);

  wire and_1_out, and_2_out, and_3_out, comparator_1_gt, comparator_2_eq, comparator_3_lt, comparator_4_eq,
       comparator_5_gt, comparator_6_eq, comparator_7_lt, comparator_8_eq, comparator_9_eq, comparator_9_gt,
       demultiplexer_1_out_0, demultiplexer_1_out_1, demultiplexer_1_out_2, demultiplexer_1_out_3,
       multiplexer_2_out, multiplexer_4_out, multiplexer_11_out, multiplexer_16_out, multiplexer_17_out,
       not_1_out, not_2_out, not_3_out, not_4_out, not_5_out, or_1_out, or_2_out, or_3_out, vga_1_p3,
       vga_1_p4;
  wire [1:0] multiplexer_1_out_2;
  wire [2:0] multiplexer_1_out_3;
  wire [15:0] alu_1_o1, eepromdualport_3_d, keyboard_1_d, multiplexer_3_out, multiplexer_5_out,
       multiplexer_6_out, multiplexer_7_out, multiplexer_8_out, multiplexer_9_out, multiplexer_10_out,
       multiplexer_12_out, multiplexer_13_out, multiplexer_14_out, multiplexer_15_out, ramdualaccess_1_d2,
       sub_1_s, vga_1_p5, vga_1_p6;
  wire [36:0] eepromdualport_1_d, multiplexer_1_out;

  EEPROMDualPort #(.AddrBits(16), .Bits(37)) eepromdualport_1 (
    .A(PC), .Din({37{1'b0}}), .str(1'b0), .C(multiplexer_2_out), .ld(1'b1), .D(eepromdualport_1_d));
  Multiplexer #(.Bits(37)) multiplexer_1 (
    .sel(not_1_out), .in_0(eepromdualport_1_d), .in_1({37{1'b0}}),
    .out({multiplexer_1_out[36:21], multiplexer_1_out_3, multiplexer_1_out[17:13], multiplexer_1_out_2, multiplexer_1_out[10:0]}));
  Multiplexer multiplexer_2 (.sel(not_1_out), .in_0(clk), .in_1(1'b0), .out(multiplexer_2_out));
  not not_1 (not_1_out, not_3_out);
  Register #(.Bits(16)) register_1 (.D(reg3), .C(clk), .en(1'b1), .Q(out_23));
  Comparator #(.Bits(16)) comparator_1 (.a(out_23), .b({16{1'b0}}), .gt(comparator_1_gt));  // open: eq, lt
  Comparator #(.Bits(16)) comparator_2 (.a(out_23), .b({16{1'b0}}), .eq(comparator_2_eq));  // open: gt, lt
  Comparator #(.Bits(16)) comparator_3 (.a(out_23), .b({16{1'b0}}), .lt(comparator_3_lt));  // open: gt, eq
  Comparator #(.Bits(16)) comparator_4 (.a(out_23), .b({16{1'b0}}), .eq(comparator_4_eq));  // open: gt, lt
  Comparator #(.Bits(16)) comparator_5 (.a(out_23), .b({16{1'b0}}), .gt(comparator_5_gt));  // open: eq, lt
  Comparator #(.Bits(16)) comparator_6 (.a(out_23), .b({16{1'b0}}), .eq(comparator_6_eq));  // open: gt, lt
  Comparator #(.Bits(16)) comparator_7 (.a(out_23), .b({16{1'b0}}), .lt(comparator_7_lt));  // open: gt, eq
  Comparator #(.Bits(16)) comparator_8 (.a(out_23), .b({16{1'b0}}), .eq(comparator_8_eq));  // open: gt, lt
  Multiplexer #(.Selector_Bits(2), .Bits(16)) multiplexer_3 (
    .sel(multiplexer_1_out[10:9]), .in_0(reg1), .in_1(reg2), .in_2(reg3), .in_3(inMem),
    .out(multiplexer_3_out));
  or or_1 (or_1_out, comparator_4_eq, comparator_5_gt);
  or or_2 (or_2_out, comparator_6_eq, comparator_7_lt);
  not not_2 (not_2_out, comparator_8_eq);
  Multiplexer #(.Selector_Bits(3)) multiplexer_4 (
    .sel(multiplexer_1_out_3), .in_0(1'b0), .in_1(comparator_1_gt), .in_2(comparator_2_eq),
    .in_3(comparator_3_lt), .in_4(or_1_out), .in_5(or_2_out), .in_6(not_2_out), .in_7(1'b1),
    .out(multiplexer_4_out));
  not not_3 (not_3_out, out_28);
  Multiplexer #(.Bits(16)) multiplexer_5 (
    .sel(multiplexer_1_out[3]), .in_0(multiplexer_1_out[36:21]), .in_1(multiplexer_3_out),
    .out(multiplexer_5_out));
  Multiplexer #(.Bits(16)) multiplexer_6 (
    .sel(multiplexer_1_out[7]), .in_0(multiplexer_5_out), .in_1(out_27), .out(multiplexer_6_out));
  Multiplexer #(.Bits(16)) multiplexer_7 (
    .sel(multiplexer_1_out[5]), .in_0(multiplexer_6_out), .in_1(memory), .out(multiplexer_7_out));
  PC pc_1 (.inc(not_3_out), .in(reg2), .load(multiplexer_4_out), .reset(1'b0), .clk(clk), .out(PC));
  Multiplexer #(.Selector_Bits(2), .Bits(16)) multiplexer_8 (
    .sel(multiplexer_1_out_2), .in_0(reg1), .in_1(reg2), .in_2(reg3), .in_3(inMem), .out(multiplexer_8_out));
  Multiplexer #(.Bits(16)) multiplexer_9 (
    .sel(multiplexer_1_out[6]), .in_0(multiplexer_12_out), .in_1(memory), .out(multiplexer_9_out));
  Multiplexer #(.Bits(16)) multiplexer_10 (
    .sel(multiplexer_1_out[4]), .in_0(multiplexer_1_out[36:21]), .in_1(multiplexer_8_out),
    .out(multiplexer_10_out));
  Multiplexer multiplexer_11 (.sel(out_28), .in_0(1'b1), .in_1(1'b0), .out(multiplexer_11_out));
  Multiplexer #(.Bits(16)) multiplexer_12 (
    .sel(multiplexer_1_out[8]), .in_0(multiplexer_10_out), .in_1(out_27), .out(multiplexer_12_out));
  ALU alu_1 (
    .a1(multiplexer_7_out), .a2(multiplexer_9_out), .neg(multiplexer_1_out[13]),
    .com(multiplexer_1_out[17:14]), .o1(alu_1_o1));
  Demultiplexer #(.Selector_Bits(2)) demultiplexer_1 (
    .sel(multiplexer_1_out[2:1]), .in(multiplexer_1_out[0]), .out_0(demultiplexer_1_out_0),
    .out_1(demultiplexer_1_out_1), .out_2(demultiplexer_1_out_2), .out_3(demultiplexer_1_out_3));
  not not_4 (not_4_out, multiplexer_1_out[0]);
  Keyboard keyboard_1 (.C(clk), .en(out_28), .D(keyboard_1_d), .av(out_28));
  and and_1 (and_1_out, not_4_out, and_2_out);
  not not_5 (not_5_out, multiplexer_1_out[1]);
  Multiplexer #(.Bits(16)) multiplexer_13 (
    .sel(out_28), .in_0({16{1'b0}}), .in_1(keyboard_1_d), .out(multiplexer_13_out));
  and and_2 (and_2_out, not_5_out, multiplexer_1_out[2]);
  Register #(.Bits(16)) register_2 (.D(alu_1_o1), .C(clk), .en(demultiplexer_1_out_0), .Q(reg1));
  Register #(.Bits(16)) register_3 (.D(alu_1_o1), .C(clk), .en(demultiplexer_1_out_1), .Q(reg2));
  Register #(.Bits(16)) register_4 (.D(alu_1_o1), .C(clk), .en(demultiplexer_1_out_2), .Q(reg3));
  Register #(.Bits(16)) register_5 (.D(alu_1_o1), .C(clk), .en(demultiplexer_1_out_3), .Q(inMem));
  Register #(.Bits(16)) register_6 (.D(alu_1_o1), .C(clk), .en(and_1_out), .Q(memory));
  and and_3 (and_3_out, multiplexer_1_out[1], not_4_out, multiplexer_1_out[2]);
  Multiplexer #(.Bits(16)) multiplexer_14 (.sel(out_28), .in_0(inMem), .in_1(16'hfde8), .out(multiplexer_14_out));
  Multiplexer #(.Bits(16)) multiplexer_15 (
    .sel(out_28), .in_0(alu_1_o1), .in_1(multiplexer_13_out), .out(multiplexer_15_out));
  Multiplexer multiplexer_16 (.sel(out_28), .in_0(and_3_out), .in_1(out_28), .out(multiplexer_16_out));
  Multiplexer multiplexer_17 (.sel(out_28), .in_0(1'b1), .in_1(1'b0), .out(multiplexer_17_out));
  EEPROMDualPort #(.AddrBits(16), .isProgramMemory("true"), .Bits(16)) eepromdualport_2 (
    .A(multiplexer_14_out), .Din(multiplexer_15_out), .str(multiplexer_16_out), .C(clk),
    .ld(multiplexer_17_out), .D(out_27));
  Comparator #(.Bits(16)) comparator_9 (
    .a(inMem), .b(16'h1b58), .gt(comparator_9_gt), .eq(comparator_9_eq));  // open: lt
  Sub #(.Bits(16)) sub_1 (.a(inMem), .b(16'h1b58), .c_i(1'b0), .s(sub_1_s));  // open: c_o
  or or_3 (or_3_out, comparator_9_gt, comparator_9_eq);
  // VGA vga_1: pin names not known; wires that end beside it: sub_1_s, clk, vga_1_p3, vga_1_p4, vga_1_p5, vga_1_p6
  RAMDualAccess #(.AddrBits(16), .isProgramMemory("true"), .Bits(16)) ramdualaccess_1 (
    .str(or_3_out), .C(clk), .ld(1'b1), .A1(sub_1_s), .Din1(out_27), .A2(vga_1_p6), .D2(ramdualaccess_1_d2));  // open: D1
  EEPROMDualPort #(.AddrBits(16), .isProgramMemory("true"), .Bits(16)) eepromdualport_3 (
    .A(vga_1_p5), .Din(out_27), .str(or_3_out), .C(clk), .ld(1'b1), .D(eepromdualport_3_d));
  VGA vga_2 (
    .R(ramdualaccess_1_d2[1:0]), .G(ramdualaccess_1_d2[3:2]), .B(ramdualaccess_1_d2[5:4]), .H(vga_1_p4),
    .V(vga_1_p3), .C(clk));

  assign out_21 = {In_Num_1, Jump, Or, And, Subtract, Add, Negate, In_Reg_2, In_Reg_1, in_FromMem_1__True, in_FromMem_1__True_2, in_Memout_1__True, in_Memout_1__True_2, In_Reg_1_True_2, In_Reg_1_True, Write_Reg, Load};

  // Notes on the sheet:
  //   clk: Hz: 2147483647
  //   contents of eepromdualport_1 (hex, n*v repeats v):
  //   80da20003,1c0000,0,220007,408c,20007,408f,402e,20007,204116,420007
  //   ,408c,20007,408f,402e,20007,204116,620007,408c,20007,408f,402e
  //   ,20007,204116,820007,408c,20007,408f,402e,20007,204116,408c,220007
  //   ,402e,20007,820001,408c,403e,20007,4089,1220003,420007,881e,420007
  //   ,408f,460f,408c,20007,408f,402e,20007,204116,20007,20808e,408f
  //   ,408c,20006,220007,408f,460f,402e,20007,408f,a402008e,408d,20007
  //   ,204116,20007,20808e,408f,408c,20006,220007,408f,20460f,402e,220007
  //   ,408f,20460f,408c,20007,408f,402e,408d,20007,204116,20007,408f
  //   ,42008e,408d,20007,204116,20007,20808e,408f,408c,20006,20029,20007
  //   ,20808e,408f,408c,20006,2002b,481d,20007,408f,2040c,402e,20007
  //   ,204116,20007,20808e,408f,408c,20006,620007,402e,20007,620007
  //   ,408f,460f,408c,20007,408f,402e,408d,20007,204116,20007,20808e
  //   ,408f,408c,20006,220007,408f,40460f,402e,220007,408f,40460f,408c
  //   ,20007,408f,402e,408d,20007,204116,220007,408f,460f,408c,20007
  //   ,408f,402e,408d,20007,204116,20007,20808e,408f,408c,20006,20029
  //   ,20007,20808e,408f,408c,20006,2002b,1881d,20007,408f,2040c,402e
  //   ,20007,204116,20007,20808e,408f,408c,20006,47c20003,80000,220007
  //   ,408f,20460f,408c,20007,408f,402e,408d,20007,204116,20007,408f
  //   ,22008e,408d,20007,204116,20007,20808e,408f,408c,20006,20029,20007
  //   ,20808e,408f,408c,20006,2002b,481d,20007,408f,2040c,402e,20007
  //   ,204116,20007,20808e,408f,408c,20006,620007,402e,20007,620007
  //   ,408f,460f,408c,20007,408f,402e,408d,20007,204116,20007,20808e
  //   ,408f,408c,20006,220007,408f,60460f,402e,20007,408f,2008e,408d
  //   ,20007,204116,220007,408f,60460f,408c,20007,408f,402e,408d,20007
  //   ,204116,20007,20808e,408f,408c,20006,620007,402e,20007,20007,20808e
  //   ,408f,408c,20006,620007,408f,460f,402e,220007,408f,460f,408c,20007
  //   ,408f,402e,408d,20007,204116,220007,408f,60460f,408c,20007,408f
  //   ,402e,408d,20007,204116,20007,408f,22008e,408d,20007,204116,20007
  //   ,20808e,408f,408c,20006,20029,20007,20808e,408f,408c,20006,2002b
  //   ,481d,20007,408f,2040c,402e,20007,204116,20007,20808e,408f,408c
  //   ,20006,620007,402e,20007,20007,20808e,408f,408c,20006,620007,408f
  //   ,460f,402e,220007,408f,60460f,408c,20007,408f,402e,408d,20007
  //   ,204116,220007,408f,460f,408c,20007,408f,402e,408d,20007,204116
  //   ,20007,408f,42008e,408d,20007,204116,20007,20808e,408f,408c,20006
  //   ,20029,20007,20808e,408f,408c,20006,2002b,481d,20007,408f,2040c
  //   ,402e,20007,204116,20007,20808e,408f,408c,20006,20029,20007,20808e
  //   ,408f,408c,20006,2002b,481d,20007,408f,2040c,402e,20007,204116
  //   ,220007,408f,20460f,408c,20007,408f,402e,408d,20007,204116,20007
  //   ,408f,22008e,408d,20007,204116,20007,20808e,408f,408c,20006,20029
  //   ,20007,20808e,408f,408c,20006,2002b,481d,20007,408f,2040c,402e
  //   ,20007,204116,20007,20808e,408f,408c,20006,620007,402e,20007,20007
  //   ,20808e,408f,408c,20006,620007,408f,460f,402e,220007,408f,40460f
  //   ,408c,20007,408f,402e,408d,20007,204116,220007,408f,460f,408c
  //   ,20007,408f,402e,408d,20007,204116,20007,408f,62008e,408d,20007
  //   ,204116,20007,20808e,408f,408c,20006,20029,20007,20808e,408f,408c
  //   ,20006,2002b,821d,20007,408f,2040c,402e,20007,204116,20007,20808e
  //   ,408f,408c,20006,20029,20007,20808e,408f,408c,20006,2002b,821d
  //   ,20007,408f,2040c,402e,20007,204116,220007,408f,20460f,408c,20007
  //   ,408f,402e,408d,20007,204116,20007,408f,42008e,408d,20007,204116
  //   ,20007,20808e,408f,408c,20006,20029,20007,20808e,408f,408c,20006
  //   ,2002b,481d,20007,408f,2040c,402e,20007,204116,20007,20808e,408f
  //   ,408c,20006,620007,402e,20007,20007,20808e,408f,408c,20006,620007
  //   ,408f,460f,402e,0,220007,408f,60460f,408c,20007,408f,402e,408d
  //   ,20007,204116,20007,408f,42008e,408d,20007,204116,20007,20808e
  //   ,408f,408c,20006,20029,20007,20808e,408f,408c,20006,2002b,481d
  //   ,20007,408f,2040c,402e,20007,204116,4c820003,1c0000,0,20007,20808e
  //   ,408f,408c,20006,20007,20808e,408f,408c,20006,20007,20808e,408f
  //   ,408c,20006,20007,20808e,408f,408c,20006,20007,20808e,408f,408c
  //   ,20006,20007,20808e,408f,408c,20006,820007,402e,20007,20808e,408f
  //   ,408c,20006,620007,402e,20007,20808e,408f,408c,20006,420007,402e
  //   ,20007,20808e,408f,408c,20006,220007,402e,20007,20808e,408f,408c
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  //   contents of eepromdualport_2 (hex, n*v repeats v):
  //   100,410,101,c,1f4,6*0,dae,1b58,1299*0,1,dac,1371,2185*0,6,6,61
  //   ,6b,75,20,6f,73,3492*0,4*46,1996,1996,0,46,1996,0,46,0,0,0,46
  //   ,0,0,0,46,9*0,4*46,0,0,0,4*46,0,10*4e,206*0,46,0,0,46,0,1996,0
  //   ,46,1996,0,46,0,0,0,46,0,0,0,46,9*0,46,0,0,46,0,0,0,46,4*0,10*4e
  //   ,206*0,4*46,1996,1996,0,46,46,46,4*0,46,0,0,0,46,9*0,46,0,0,46
  //   ,0,0,0,4*46,0,10*4e,206*0,46,0,0,46,0,0,0,46,1996,0,46,0,0,0,46
  //   ,0,0,0,46,9*0,46,0,0,46,6*0,46,0,10*4e,206*0,1996,0,0,1996,1996,1996
  //   ,0,46,1996,0,46,0,0,0,5*46,9*0,4*46,0,0,0,4*46,0,10*4e,246*0,10*4e
  //   ,246*0,10*4e,246*0,10*4e,206*0,4*1996,0,1996,0,0,1996,31*0,10*4e
  //   ,209*0,1996,0,1996,0,0,1996,31*0,10*4e,206*0,4*1996,0,1996,0,0
  //   ,1996,250*0,1996,0,1996,0,0,1996,247*0,4*1996,0,1996,0,0,1996
  //   ,1015*0,1996,0,1996,0,4*1996,0,1996,1996,1996,244*0,1996,0,1996
  //   ,4*0,1996,0,0,0,1996,244*0,1996,1996,1996,0,4*1996,0,1996,1996,1996
  //   ,246*0,1996,4*0,1996,0,1996,248*0,1996,0,4*1996,0,1996,1996,1996
  //   ,20638*0,5,32764*0,ffff
  //   contents of eepromdualport_3 (hex, n*v repeats v):
  //   4*46,1996,1996,ffff,46,1996,1996,46,1996,ffff,ffff,46,ffff,ffff,ffff
  //   ,46,9*ffff,4*46,ffff,ffff,ffff,4*46,ffff,10*4e,20*0,4*ffff,0,4*ffff
  //   ,177*0,46,ffff,0,46,ffff,1996,ffff,46,1996,ffff,46,1996,ffff,ffff
  //   ,46,ffff,ffff,ffff,46,7*ffff,0,ffff,46,0,ffff,46,ffff,ffff,ffff
  //   ,46,0,ffff,ffff,ffff,10*4e,ffff,0,ffff,ffff,0,ffff,0,0,ffff,0
  //   ,ffff,ffff,0,ffff,0,ffff,0,0,ffff,0,ffff,0,0,ffff,0,ffff,0,0,ffff
  //   ,177*0,4*46,1996,1996,ffff,46,46,46,1996,1996,ffff,ffff,46,ffff,ffff,ffff
  //   ,46,9*ffff,46,ffff,ffff,46,ffff,ffff,ffff,4*46,ffff,10*4e,4*ffff
  //   ,0,4*ffff,0,4*ffff,0,4*ffff,0,4*ffff,0,4*ffff,177*0,46,ffff,0
  //   ,46,ffff,ffff,ffff,46,1996,ffff,46,1996,ffff,ffff,46,ffff,ffff,ffff
  //   ,46,7*ffff,0,ffff,46,0,ffff,46,4*ffff,0,ffff,46,ffff,10*4e,4*ffff
  //   ,0,ffff,0,0,ffff,0,ffff,ffff,0,ffff,0,ffff,0,0,ffff,0,ffff,0,0
  //   ,ffff,0,ffff,0,0,ffff,177*0,1996,0,0,1996,1996,1996,0,46,1996,1996
  //   ,46,1996,0,0,5*46,9*0,4*46,0,0,0,4*46,0,10*4e,246*0,10*4e,206*0
  //   ,4*ffff,0,4*ffff,0,4*ffff,0,4*ffff,0,4*ffff,0,4*ffff,0,4*ffff
  //   ,0,4*ffff,0,10*4e,4*ffff,0,4*ffff,0,4*ffff,0,4*ffff,0,4*ffff,0
  //   ,4*ffff,177*0,ffff,0,0,ffff,0,ffff,0,0,ffff,0,ffff,0,0,ffff,0
  //   ,ffff,0,0,ffff,0,ffff,0,0,ffff,0,ffff,0,0,ffff,0,ffff,0,0,ffff
  //   ,0,ffff,0,0,ffff,0,10*4e,ffff,0,0,ffff,0,ffff,0,0,ffff,0,ffff
  //   ,0,0,ffff,0,ffff,0,0,ffff,0,ffff,0,0,ffff,0,ffff,0,0,ffff,177*0
  //   ,6*1996,ffff,ffff,1996,0,4*ffff,0,4*ffff,0,4*ffff,0,4*ffff,0,4*ffff
  //   ,0,4*ffff,0,10*4e,4*ffff,0,4*ffff,0,4*ffff,0,4*ffff,0,4*ffff,0
  //   ,4*ffff,177*0,1996,0,0,1996,0,1996,0,0,1996,0,ffff,0,0,ffff,0
  //   ,ffff,0,0,ffff,0,ffff,0,0,ffff,0,ffff,0,0,ffff,0,ffff,0,0,ffff
  //   ,0,ffff,0,0,ffff,0,10*4e,ffff,0,0,ffff,0,ffff,0,0,ffff,0,ffff
  //   ,0,0,ffff,0,ffff,0,0,ffff,0,ffff,0,0,ffff,0,ffff,0,0,ffff,177*0
  //   ,6*1996,0,0,1996,247*0,1996,0,0,1996,0,1996,0,0,1996,247*0,6*1996
  //   ,ffff,ffff,1996,0,4*ffff,0,4*ffff,0,4*ffff,0,4*ffff,0,4*ffff,0
  //   ,4*ffff,0,4*ffff,212*0,ffff,0,0,ffff,0,ffff,0,0,ffff,0,ffff,0,0
  //   ,ffff,0,ffff,0,0,ffff,0,ffff,0,0,ffff,0,ffff,0,0,ffff,0,ffff,0,0
  //   ,ffff,0,ffff,0,0,ffff,0,ffff,0,0,ffff,212*0,4*ffff,0,4*ffff,0
  //   ,4*ffff,0,4*ffff,0,4*ffff,0,4*ffff,0,4*ffff,0,4*ffff,0,4*ffff
  //   ,212*0,ffff,0,0,ffff,0,ffff,0,0,ffff,0,ffff,0,0,ffff,0,ffff,0,0
  //   ,ffff,0,ffff,0,0,ffff,0,ffff,0,0,ffff,0,ffff,0,0,ffff,0,ffff,0,0
  //   ,ffff,0,ffff,0,0,ffff,212*0,1996,0,10*1996,244*0,1996,0,1996,0,0
  //   ,1996,0,1996,0,0,0,1996,244*0,12*1996,244*0,1996,0,1996,1996,0,0,0
  //   ,1996,0,1996,0,1996,244*0,1996,0,10*1996,25638*0,5,27764*0,ffff
  //   ,4999*0,ffff
endmodule
