// Digital circuit VGA.dig as structural Verilog
module VGA (
  input  [15:0] Adress,
  input  clock,
  output VS,
  output HS,
  output [15:0] outAdress,
  output [15:0] coloro
);

  wire and_1_out, and_2_out, and_3_out, comparator_1_lt, comparator_2_eq, comparator_2_gt, comparator_3_eq,
       comparator_4_lt, comparator_5_eq, comparator_5_gt, comparator_6_lt, comparator_7_lt, comparator_8_eq,
       or_1_out, or_2_out;
  wire [15:0] add_1_s, add_2_s, add_3_s, add_4_s, add_5_s, counterpreset_1_out, counterpreset_2_out, sub_1_s,
       sub_2_s;

  Add #(.Bits(16)) add_1 (.a(add_2_s), .b({16{1'b1}}), .c_i(1'b0), .s(add_1_s));  // open: c_o
  Add #(.Bits(16)) add_2 (.a(16'hfff6), .b(add_3_s), .c_i(1'b0), .s(add_2_s));  // open: c_o
  Add #(.Bits(16)) add_3 (.a(16'hffdf), .b(16'hfffe), .c_i(1'b0), .s(add_3_s));  // open: c_o
  Add #(.Bits(16)) add_4 (.a(16'hfff0), .b(add_5_s), .c_i(1'b0), .s(add_4_s));  // open: c_o
  Add #(.Bits(16)) add_5 (.a(16'hffd0), .b(16'hffa0), .c_i(1'b0), .s(add_5_s));  // open: c_o
  Sub #(.Bits(16)) sub_1 (.a(16'h280), .b(16'h1), .c_i(1'b0), .s(sub_1_s));  // open: c_o
  Comparator #(.Bits(16)) comparator_1 (
    .a({counterpreset_1_out[15:11], coloro[7:0], counterpreset_1_out[2:0]}), .b(16'hffd0),
    .lt(comparator_1_lt));  // open: gt, eq
  Comparator #(.Bits(16)) comparator_2 (
    .a({counterpreset_1_out[15:11], coloro[7:0], counterpreset_1_out[2:0]}), .b(add_5_s),
    .gt(comparator_2_gt), .eq(comparator_2_eq));  // open: lt
  Sub #(.Bits(16)) sub_2 (.a(16'h1e0), .b(16'h1), .c_i(1'b0), .s(sub_2_s));  // open: c_o
  Comparator #(.Bits(16)) comparator_3 (
    .a({counterpreset_1_out[15:11], coloro[7:0], counterpreset_1_out[2:0]}), .b(sub_1_s), .eq(comparator_3_eq));  // open: gt, lt
  Comparator #(.Bits(16)) comparator_4 (
    .a({counterpreset_2_out[15:11], coloro[15:8], counterpreset_2_out[2:0]}), .b(16'hffdf),
    .lt(comparator_4_lt));  // open: gt, eq
  Comparator #(.Bits(16)) comparator_5 (
    .a({counterpreset_2_out[15:11], coloro[15:8], counterpreset_2_out[2:0]}), .b(add_3_s),
    .gt(comparator_5_gt), .eq(comparator_5_eq));  // open: lt
  CounterPreset #(.Bits(16)) counterpreset_1 (
    .en(1'b1), .C(clock), .dir(1'b0), .in(add_4_s), .ld(comparator_3_eq), .clr(1'b0),
    .out({counterpreset_1_out[15:11], coloro[7:0], counterpreset_1_out[2:0]}));  // open: ovf
  or or_1 (or_1_out, comparator_2_gt, comparator_2_eq);
  Comparator #(.Bits(16)) comparator_6 (
    .a({counterpreset_1_out[15:11], coloro[7:0], counterpreset_1_out[2:0]}), .b(16'h280), .lt(comparator_6_lt));  // open: gt, eq
  Comparator #(.Bits(16)) comparator_7 (
    .a({counterpreset_2_out[15:11], coloro[15:8], counterpreset_2_out[2:0]}), .b(16'h1e0),
    .lt(comparator_7_lt));  // open: gt, eq
  CounterPreset #(.Bits(16)) counterpreset_2 (
    .en(comparator_3_eq), .C(clock), .dir(1'b0), .in(add_1_s), .ld(comparator_8_eq), .clr(1'b0),
    .out({counterpreset_2_out[15:11], coloro[15:8], counterpreset_2_out[2:0]}));  // open: ovf
  Comparator #(.Bits(16)) comparator_8 (
    .a({counterpreset_2_out[15:11], coloro[15:8], counterpreset_2_out[2:0]}), .b(sub_2_s),
    .eq(comparator_8_eq));  // open: gt, lt
  and and_1 (and_1_out, comparator_6_lt, comparator_7_lt);
  or or_2 (or_2_out, comparator_5_gt, comparator_5_eq);
  and and_2 (and_2_out, comparator_1_lt, or_1_out);
  and and_3 (and_3_out, comparator_4_lt, or_2_out);
  xor xor_1 (HS, and_2_out, 1'b1);
  xor xor_2 (VS, and_3_out, 1'b1);
  // Pins of 1 and 16 bits meet at coloro

  assign outAdress = Adress;
endmodule
